# Fritzing sketch Burnell bot (saved by Fritzing 0.9.2b)
circuit board: 8.46667cm x 5.64444cm
breadboards: 1

parts:
  U1 = ESP8266 WiFi Module [part_number=ESP8266]
  Part1 = BH1750
  DHT1 = DHT22 Humidity and Temperature Sensor
  PIR1 = PIR sensor
  U2 = DSUN-DC Adapter
  C1 = Electrolytic Capacitor [package="300 mil [THT, electrolytic]"]
  R1 = Resistor [tolerance=±5% resistance=1k package="0402 [SMD]"]

nets:
  VCC: U1.VCC, U1.GPIO_2, U1.CH_PD, Part1.VCC, DHT1.VDD, PIR1.VDD, U2.VCC_OUT, C1.+, R1.Pin_0
  GND: U1.GND, U1.GPIO_15, Part1.GND, DHT1.GND, PIR1.GND, U2.GND_OUT, C1.-
  N1: U1.GPIO_4, Part1.SDA
  N2: U1.GPIO_5, Part1.SCL
  N3: U1.GPIO_14, DHT1.DATA, R1.Pin_1
  N4: U1.GPIO_12, PIR1.SIG

notes:
  3.3v Power supply
  NB: Layout of pads on ESP is wrong on this illustration! Pin numbers correct in schematic.
  GPIO5 -> SCL
  GPIO4 -> SDA

custom parts:
  ESP8266 WiFi Module: Generic WiFi Module based on the ESP8266 with onboard PCB antenna and UART communications
  BH1750: Light Sensor
  DSUN-DC Adapter: DSUN-DC Adapter with variable input/output
  Electrolytic Capacitor: 2200µF electrolytic capacitor
